# Fritzing sketch 16x2 Display - Raspberry pi4 (saved by Fritzing 0.8.7b)
breadboards: 1

parts:
  Raspberry_Pi_1 = Raspberry Pi 4 [part_number=RPI-4-b]
  LCD1 = LCD screen
  R1 = Rotary Potentiometer (Small) [maximum_resistance=100kΩ package=THT]
  R2 = Rotary Potentiometer (Small) [maximum_resistance=100kΩ package=THT]

nets:
  N1: Raspberry_Pi_1.GPIO4, LCD1.RS
  N2: Raspberry_Pi_1.GPIO17, LCD1.E
  N3: Raspberry_Pi_1.GPIO27, LCD1.DB5
  N4: Raspberry_Pi_1.GPIO23, LCD1.DB7
  GND: Raspberry_Pi_1.GND, LCD1.VSS, LCD1.R/W, LCD1.DB6, LCD1.LED-, R1.wiper
  N5: Raspberry_Pi_1.GPIO18, LCD1.DB4
  5V: Raspberry_Pi_1.5V, LCD1.VDD, R2.wiper
  N6: LCD1.V0, R1.leg1
  N7: LCD1.LED+, R2.leg1

custom parts:
  Raspberry Pi 4: The RPi4, a faster version of the awesome Raspberry Pi 2 B ARM Board with 40 pin gpio. Ready for special Raspberry Pi B+ and RPi2 Hat (Hardware attached (on) top)
